// Logisim project DDCA EXPO TOPIC.circ as structural Verilog: 1 circuit, main circuit main
// CLK
module main (
  input  D3,
  input  PR,
  input  CLR,
  output Q7,
  output Q6,
  output Q5,
  output Q4,
  output Q3,
  output Q2,
  output Q1,
  output Q0
);

  wire CLK_out, d_ff_4_qn;

  Clock CLK (.out(CLK_out));
  D_Flip_Flop d_ff_1 (.clk(CLK_out), .D(D3), .Q(Q7), .preset(PR), .reset(CLR));  // open: Qn, en
  D_Flip_Flop d_ff_2 (.clk(CLK_out), .D(Q7), .Q(Q6), .preset(PR), .reset(CLR));  // open: Qn, en
  D_Flip_Flop d_ff_3 (.clk(CLK_out), .D(Q6), .Q(Q5), .preset(PR), .reset(CLR));  // open: Qn, en
  D_Flip_Flop d_ff_4 (.clk(CLK_out), .D(Q5), .Q(Q4), .Qn(d_ff_4_qn), .preset(PR), .reset(CLR));  // open: en
  D_Flip_Flop d_ff_5 (.clk(CLK_out), .Q(Q3), .preset(PR), .reset(CLR));  // open: D, Qn, en
  D_Flip_Flop d_ff_6 (.clk(CLK_out), .D(Q3), .Q(Q2), .preset(PR), .reset(CLR));  // open: Qn, en
  D_Flip_Flop d_ff_7 (.clk(CLK_out), .D(Q2), .Q(Q1), .preset(PR), .reset(CLR));  // open: Qn, en
  D_Flip_Flop d_ff_8 (.clk(CLK_out), .D(Q1), .Q(Q0), .preset(PR), .reset(CLR));  // open: Qn, en

  // Notes on the sheet:
  //   DEF7
  //   DEF6
  //   DEF5
  //   DEF4
  //   DEF3
  //   DEF2
  //   DEF1
  //   DEF0
endmodule
