// Logisim project fulladder.circ as structural Verilog: 1 circuit, main circuit main
module main (
  input  A,
  input  B,
  input  C_in,
  output SUM,
  output C_OUT
);

  wire and_1_out, xor_1_out;

  and and_1 (and_1_out, A, B);
  xor xor_1 (xor_1_out, A, B);
  and and_2 (xor_1_out, xor_1_out, and_1_out);
  xor xor_2 (SUM, xor_1_out, C_in);
  or or_1 (C_OUT, xor_1_out, C_in);

  // Notes on the sheet:
  //   XOR_!
  //   C_in
  //   AND1
  //   C1
  //   S1
  //   XOR_2
  //   AND 2
  //   C2
endmodule
